# Fritzing sketch power_metter_ina219 (saved by Fritzing 0.9.1b)
breadboards: 1

parts:
  INA1 = INA219 DC Current Sensor Breakout
  Part1 = Arduino Pro Mini v13

nets:
  VCC: INA1.VCC, Part1.VCC
  GND: INA1.GND, Part1.GND
  N1: INA1.SCL, Part1.A5
  N2: INA1.SDA, Part1.A4

custom parts:
  INA219 DC Current Sensor Breakout: INA DC Current Sensor Breakout
